# Fritzing sketch rodOK (saved by Fritzing 0.9.3b)
circuit board: 4cm x 6cm

parts:
  M3 = male pin header, 2 pins [form="♂ (male)"]
  M4 = male pin header, 2 pins [form="♂ (male)"]
  M5 = male pin header, 2 pins [form="♂ (male)"]
  M6 = male pin header, 4 pins [form="♂ (male)"]
  M7 = male pin header, 4 pins [form="♂ (male)"]
  M8 = male pin header, 4 pins [form="♂ (male)"]
  M1 = male pin header, 1 pin [form="♂ (male)"]
  BlueM = male pin header, 4 pins [form="♂ (male)"]
  M10 = male pin header, 5 pins [form="♂ (male)"]
  Componente1 = Arduino Nano (Rev3.0)
  M11 = male pin header, 4 pins [form="♂ (male)"]
  M2 = male pin header, 9 pins [form="♂ (male)"]
  M12 = molex pin header, 2 pins [form=molex]

nets:
  N1: M3.pin1, M5.pin1, M6.pin2, M8.pin1, M8.pin2, M8.pin3, M8.pin4, BlueM.pin2, Componente1.5V, M11.pin1
  N2: M3.pin2, M4.pin2, M6.pin1, M7.pin1, M7.pin2, M7.pin3, M7.pin4, BlueM.pin1, Componente1.GND, M11.pin2, M12.pin1
  N3: M4.pin1, M5.pin2, M12.pin2
  N4: M6.pin3, Componente1.A5
  N5: M6.pin4, Componente1.A4
  N6: M1.pin1, Componente1.VIN
  N7: BlueM.pin3, Componente1.A7
  N8: BlueM.pin4, Componente1.A6
  N9: M10.pin1, Componente1.D13/SCK
  N10: M10.pin2, Componente1.A0
  N11: M10.pin3, Componente1.A1
  N12: M10.pin4, Componente1.A2
  N13: M10.pin5, Componente1.A3
  N14: Componente1.D2, M11.pin3
  N15: Componente1.D3, M11.pin4
  N16: Componente1.D4, M2.pin9
  N17: Componente1.D5, M2.pin8
  N18: Componente1.D6, M2.pin7
  N19: Componente1.D7, M2.pin6
  N20: Componente1.D8, M2.pin5
  N21: Componente1.D9, M2.pin4
  N22: Componente1.D10, M2.pin3
  N23: Componente1.D11/MOSI, M2.pin2
  N24: Componente1.D12/MISO, M2.pin1
